# Fritzing sketch MQTTletterbox (saved by Fritzing 0.9.3b)
breadboards: 1

parts:
  IC1 = Adafruit Feather HUZZAH ESP8266 [part_number="Adafruit #2821"]
  SENS1 = AM2302 Humidity and Temperature Sensor
  SENS2 = GP2Y0D810Z0F Digital Distance Sensor
  S1 = Tilt Switch [package=THT]
  IC2 = Adafruit TSL2561 [part_number="Adafruit #439"]

nets:
  N1: IC1.GPIO12/MISO, S1.Pin_1
  N2: IC1.GPIO13/MOSI, S1.Pin_2
  N3: IC1.GPIO14/SCK, SENS2.OUT
  GND: IC1.GND, SENS1.GND, SENS2.GND, IC2.GND
  VIN: IC1.3.3V, SENS1.VDD, SENS2.VIN, IC2.VIN
  N4: IC1.GPIO0, SENS1.DATA
  N5: IC1.GPIO5/SCL, IC2.SCL
  N6: IC1.GPIO4/SDA, IC2.SDA

custom parts:
  Adafruit Feather HUZZAH ESP8266: his is the Adafruit Feather HUZZAH ESP8266 - our take on an 'all-in-one' ESP8266 WiFi development board with built in USB and battery charging. Its an ESP8266 WiFi module with all the extras you need, ready to rock! We have other boards in the Feather family, check'em out here. At the Feather HUZZAH's heart is an ESP8266 WiFi microcontroller clocked at 80 MHz and at 3.3V logic. This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
  Adafruit TSL2561: The TSL2561 luminosity sensor is an advanced digital light sensor, ideal for use in a wide range of light situations. Compared to low cost CdS cells, this sensor is more precise, allowing for exact lux calculations and can be configured for different gain/timing ranges to detect light ranges from up to 0.1 - 40,000+ Lux on the fly. The best part of this sensor is that it contains both infrared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
